# Fritzing sketch firtziz (saved by Fritzing 0.9.3b)
breadboards: 1

parts:
  LED1 = smd LED [color="Red (633nm)" package="1206 [SMD]"]
  LED7 = smd LED [color="Red (633nm)" package="1206 [SMD]"]
  LED9 = smd LED [color="Red (633nm)" package="1206 [SMD]"]
  LED10 = smd LED [color="Red (633nm)" package="1206 [SMD]"]
  LED11 = smd LED [color="Red (633nm)" package="1206 [SMD]"]
  LED12 = smd LED [color="Red (633nm)" package="1206 [SMD]"]
  LED13 = smd LED [color="Red (633nm)" package="1206 [SMD]"]
  LED14 = smd LED [color="Red (633nm)" package="1206 [SMD]"]
  LED15 = smd LED [color="Red (633nm)" package="1206 [SMD]"]
  LED16 = smd LED [color="Red (633nm)" package="1206 [SMD]"]
  Composant1 = Arduino Uno (Rev3)
  R11 = Resistor [tolerance=±5% resistance=220 package=THT]
  R12 = Resistor [tolerance=±5% resistance=220 package=THT]
  R13 = Resistor [tolerance=±5% resistance=220 package=THT]
  R14 = Resistor [tolerance=±5% resistance=220 package=THT]
  R15 = Resistor [tolerance=±5% resistance=220 package=THT]
  R16 = Resistor [tolerance=±5% resistance=220 package=THT]
  R17 = Resistor [tolerance=±5% resistance=220 package=THT]
  R18 = Resistor [tolerance=±5% resistance=220 package=THT]
  R19 = Resistor [tolerance=±5% resistance=220 package=THT]
  R20 = Resistor [tolerance=±5% resistance=220 package=THT]

nets:
  N1: LED1.cathode, Composant1.D7
  N2: LED1.anode, R18.Pin_0
  N3: LED7.cathode, Composant1.D4
  N4: LED7.anode, R13.Pin_1
  N5: LED9.cathode, Composant1.D5_PWM
  N6: LED9.anode, R12.Pin_0
  N7: LED10.cathode, Composant1.D6_PWM
  N8: LED10.anode, R11.Pin_0
  N9: LED11.cathode, Composant1.D3_PWM
  N10: LED11.anode, R14.Pin_1
  N11: LED12.cathode, Composant1.D2
  N12: LED12.anode, R15.Pin_1
  N13: LED13.cathode, Composant1.D10_PWM/SS
  N14: LED13.anode, R16.Pin_0
  N15: LED14.cathode, Composant1.D9_PWM, R20.Pin_0
  N16: LED15.cathode, Composant1.D8
  N17: LED15.anode, R19.Pin_0
  N18: LED16.anode, R17.Pin_0
  N19: Composant1.GND, R11.Pin_1, R12.Pin_1, R13.Pin_0, R14.Pin_0, R15.Pin_0, R16.Pin_1, R17.Pin_1, R18.Pin_1, R19.Pin_1, R20.Pin_1
